# Fritzing sketch serialGoalNew (saved by Fritzing 0.9.3b)
perfboards: 1

parts:
  U1 = ESP32-38PinWide [part_number=ESP32-38PinWide]
  Battery = 4 x AAA Battery Mount  # not connected
  LD1 = LD  # not connected
  Part2 = KY-018 Photoresistor Module [package="Breakout board"]
  Raspberry_Pi_1 = Raspberry Pi 3 [part_number=RPI-3-V1.2]  # not connected
  Q1 = MOSFET-NCHANNEL [package=to-92]  # not connected

nets:
  N1: U1.GPIO1, Part2.Vin

custom parts:
  ESP32-38PinWide: Generic 38-Pin ESP32 with wide format (only access to one side of pins on a breadboard) based on Stephen Lilley's HiLetgo ESP-WROOM-32 ESP32 ESP-32S Development Board.
  LD: A Generic Red Dot Laser Diode Module (~5mW)
  KY-018 Photoresistor Module: KY-018 Photoresistor module, used to measure light intensity. It can determine the presence or absence of light.
